# Fritzing sketch Scheme (saved by Fritzing 0.9.3b)
breadboards: 1

parts:
  Raspberry_Pi_1 = Raspberry Pi 3 [part_number=RPI-3-V1.2]
  LED1 = RGB LED (com. anode, rbg) [package="5 mm [THT]"]
  R1 = Resistor [tolerance=±5% resistance=220 package=THT]
  R2 = Resistor [tolerance=±5% resistance=220 package=THT]
  R3 = Resistor [tolerance=±5% resistance=220 package=THT]
  U1 = SWITCH_SPDT [package=kps-1290]
  R4 = Resistor [tolerance=±5% resistance=1k package=THT]
  RHT1 = Humidity and Temperature Sensor RHT03
  R5 = Resistor [tolerance=±5% resistance=10k package="2512 [SMD]"]
  SP1 = SPEAKER [package=pcb_mount_speaker]  # not connected
  USB_Microphone = Breakout Board for Electret Microphone  # not connected

nets:
  N1: Raspberry_Pi_1.GIPO4, U1.P
  N2: Raspberry_Pi_1.GIPO17, RHT1.Data-signal, R5.Pin_1
  N3: Raspberry_Pi_1.GIPO13, R3.Pin_0
  N4: Raspberry_Pi_1.GIPO19, R2.Pin_0
  N5: Raspberry_Pi_1.GIPO26, R1.Pin_0
  N6: Raspberry_Pi_1.GND, R4.Pin_0, RHT1.GND_2
  5V: Raspberry_Pi_1.5V, LED1.common_anode, U1.O, RHT1.Vcc, R5.Pin_0
  N7: LED1.red_cathode, R1.Pin_1
  N8: LED1.blue_cathode, R2.Pin_1
  N9: LED1.green_cathode, R3.Pin_1
  N10: U1.S, R4.Pin_1

notes:
  Usb Microphone
  Speaker
